# Fritzing sketch waterfall (saved by Fritzing 0.9.3b)
breadboards: 1

parts:
  Part1 = Arduino Uno (Rev3)
  Part2 = Bluetooth HC-05 Macho
  M1 = DC Motor
  S1 = Round Pushbutton
  S2 = Round Pushbutton
  L298N1 = L298N DC motor driver
  R1 = Resistor [tolerance=±5% resistance=10k package="2010 [SMD]"]
  R2 = Resistor [tolerance=±5% resistance=10k package="2010 [SMD]"]
  R3 = Resistor [tolerance=±5% resistance=1k package="2010 [SMD]"]
  R4 = Resistor [tolerance=±5% resistance=330 package="2010 [SMD]"]
  Power_plug1 = Power plug

nets:
  N1: Part1.D8, R3.Pin_0
  N2: Part1.D10_PWM/SS, L298N1.IN1
  N3: Part1.D11_PWM/MOSI, L298N1.IN2
  N4: Part1.D2, S1.leg1, R2.Pin_1
  N5: Part1.D3_PWM, S2.leg1, R1.Pin_1
  N6: Part1.D7, Part2.TXD
  5V: Part1.5V, Part2.VCC, S1.leg0, S2.leg0
  GND: Part1.GND, Part2.GND, L298N1.GND, R1.Pin_0, R2.Pin_0, R4.Pin_0, Power_plug1.GND
  N7: Part2.RXD, R3.Pin_1, R4.Pin_1
  N8: M1.pin_1, L298N1.OUT2
  N9: M1.pin_2, L298N1.OUT1
  12V: L298N1.12V, Power_plug1.VCC

notes:
  12v
  Bomba d'água
  Sensores de nível de água

custom parts:
  L298N DC motor driver: 2x DC motor driver with 78M05 positive voltage regulator (7..35 V) L298N: max 46 V, 2 A Set 5 V Enable jumper to enable 5 V regultor (needed for the L298N) and +5 V output at screw terminal or supply external +5 V at screw terminal Set ENA and/or ENB to +5 V to enable motor permanently or supply ENA and/or ENB with PWM signal IN1 and IN2 set rotation directory for motor A (OUT1/OUT2) IN2 and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
